# Fritzing sketch circuito_portao (saved by Fritzing 0.9.3b)
breadboards: 1

parts:
  M1 = DC Motor
  Power_plug1 = Power plug
  OMRON1 = OMRON PCB Power Relay – G5LE [part_number="G5LE-1\n" package=THT]
  OMRON2 = OMRON PCB Power Relay – G5LE [part_number="G5LE-1\n" package=THT]
  Part1 = Arduino Uno (Rev3)  # not connected

nets:
  N1: M1.pin_1, OMRON1.C
  N2: M1.pin_2, OMRON2.C
  N3: Power_plug1.GND, OMRON1.A, OMRON2.B
  N4: Power_plug1.VCC, OMRON1.B, OMRON2.A
